# Fritzing sketch not gates (saved by Fritzing 0.9.4)
breadboards: 1

parts:
  U1 = SN74LS14N [package="DIP14 [THT]"]
  VCC1 = Battery
  LED1 = LED - 5mm [color="Red (633nm)" package="5 mm [THT]"]
  R1 = Resistor [tolerance=±5% resistance=220 package="1206 [SMD]"]

nets:
  N1: U1.1A, U1.4Y
  N2: U1.1Y, U1.2A
  N3: U1.2Y, U1.3A
  N4: U1.3Y, LED1.anode
  N5: U1.GND, VCC1.-, R1.Pin_1
  N6: U1.4A, U1.5Y
  N7: U1.5A, U1.6Y
  N8: U1.6A, U1.VCC, VCC1.+
  N9: LED1.cathode, R1.Pin_0
